// Logisim project FA.circ as structural Verilog: 2 circuits, main circuit FA
module FA (
  input  A,
  input  B,
  input  CIN,
  output S,
  output COUT
);

  wire and_1_out, and_2_out, xor_1_out;

  and and_1 (and_1_out, B, A);
  xor xor_1 (xor_1_out, B, A);
  xor xor_2 (S, xor_1_out, CIN);
  and and_2 (and_2_out, xor_1_out, CIN);
  or or_1 (COUT, and_1_out, and_2_out);
endmodule

module ADDSUB4 (
  input  SUB,
  input  [3:0] A,
  input  [3:0] B,
  output Z,
  output C1,
  output [3:0] S,
  output C2,
  output N,
  output COUT,
  output C3
);

  wire fa_1_cout, xor_1_out, xor_2_out, xor_3_out, xor_4_out;

  xor xor_1 (xor_1_out, B[0], SUB);
  xor xor_2 (xor_2_out, B[1], SUB);
  xor xor_3 (xor_3_out, B[2], SUB);
  xor xor_4 (xor_4_out, B[3], SUB);
  FA fa_1 (.A(A[0]), .B(xor_1_out), .CIN(SUB), .S(S[0]), .COUT(fa_1_cout));
  FA fa_2 (.A(A[1]), .B(xor_2_out), .CIN(fa_1_cout), .S(S[1]), .COUT(C1));
  FA fa_3 (.A(A[2]), .B(xor_3_out), .CIN(C1), .S(S[2]), .COUT(C2));
  FA fa_4 (.A(A[3]), .B(xor_4_out), .CIN(C2), .S(N), .COUT(C3));
  nor nor_1 (Z, S[0], S[1], S[2], N);

  assign COUT = C3;
  assign S[3] = N;
endmodule
