// Logisim project TN3.circ as structural Verilog: 3 circuits, main circuit main
module main (
  input  D,
  input  CLK,
  output Q1,
  output Q2,
  output Q3,
  output DLATCH2,
  output FLIPFLOP2
);

  wire dff_ms_2_q, dlatch_2_q;

  D_Flip_Flop d_ff_1 (.D(D), .clk(CLK), .Q(Q2));  // open: Qn, preset, reset
  DLATCH dlatch_1 (.D(D), .E(CLK), .Q(Q1));
  DFF_MS dff_ms_1 (.D(D), .CLK(CLK), .Q(Q3));
  DLATCH dlatch_2 (.D(D), .E(CLK), .Q(dlatch_2_q));
  DFF_MS dff_ms_2 (.D(D), .CLK(CLK), .Q(dff_ms_2_q));
  DLATCH dlatch_3 (.D(dlatch_2_q), .E(CLK), .Q(DLATCH2));
  DFF_MS dff_ms_3 (.D(dff_ms_2_q), .CLK(CLK), .Q(FLIPFLOP2));
endmodule

module DLATCH (
  input  D,
  input  E,
  output Q
);

  Multiplexer multiplexer_1 (.in0(Q), .in1(D), .out(Q), .sel(E));
endmodule

module DFF_MS (
  input  D,
  input  CLK,
  output Q
);

  wire dlatch_1_q, not_1_out;

  not not_1 (not_1_out, CLK);
  DLATCH dlatch_1 (.D(D), .E(not_1_out), .Q(dlatch_1_q));
  DLATCH dlatch_2 (.D(dlatch_1_q), .E(CLK), .Q(Q));
endmodule
