// Logisim project TN4.circ as structural Verilog
module REGFILE (
  input  CLK,
  input  WE,
  input  [1:0] RD,
  input  [7:0] DIN,
  input  [1:0] RA,
  input  [1:0] RB,
  output [7:0] R0,
  output [7:0] R1,
  output [7:0] QA,
  output [7:0] R2,
  output [7:0] QB,
  output [7:0] R3
);

  wire decoder_1_out0, decoder_1_out1, decoder_1_out2, decoder_1_out3;

  Decoder #(.select(2)) decoder_1 (
    .out0(decoder_1_out0), .out1(decoder_1_out1), .out2(decoder_1_out2), .out3(decoder_1_out3), .sel(RD),
    .en(WE));
  Register register_1 (.D(DIN), .en(decoder_1_out0), .clk(CLK), .Q(R0));  // open: clr
  Register register_2 (.D(DIN), .en(decoder_1_out1), .clk(CLK), .Q(R1));  // open: clr
  Register register_3 (.D(DIN), .en(decoder_1_out2), .clk(CLK), .Q(R2));  // open: clr
  Register register_4 (.D(DIN), .en(decoder_1_out3), .clk(CLK), .Q(R3));  // open: clr
  Multiplexer #(.select(2), .width(8)) multiplexer_1 (.in0(R0), .in1(R1), .in2(R2), .in3(R3), .out(QA), .sel(RA));
  Multiplexer #(.select(2), .width(8)) multiplexer_2 (.in0(R0), .in1(R1), .in2(R2), .in3(R3), .out(QB), .sel(RB));
endmodule

module DATAPATH (
  input  CLK,
  input  SRC,
  input  [2:0] OP,
  input  [7:0] IMM,
  input  [1:0] RA,
  input  [1:0] RB,
  input  [1:0] RD,
  input  WE,
  output [7:0] R0,
  output [7:0] R1,
  output [7:0] R,
  output [7:0] R2,
  output [7:0] R3,
  output Z
);

  wire [7:0] multiplexer_1_out, regfile_1_qa, regfile_1_qb;

  REGFILE regfile_1 (
    .CLK(CLK), .WE(WE), .RD(RD), .DIN(multiplexer_1_out), .RA(RA), .RB(RB), .R0(R0), .R1(R1),
    .QA(regfile_1_qa), .R2(R2), .QB(regfile_1_qb), .R3(R3));
  ALU8 alu8_1 (.A(regfile_1_qa), .B(regfile_1_qb), .OP(OP), .R(R), .Z(Z));
  Multiplexer #(.width(8)) multiplexer_1 (.in0(R), .in1(IMM), .out(multiplexer_1_out), .sel(SRC));
endmodule

module ALU8 (
  input  [7:0] A,
  input  [7:0] B,
  input  [2:0] OP,
  output [7:0] R,
  output Z
);

  wire [7:0] adder_1_out, adder_2_out, and_1_out, multiplexer_1_out, multiplexer_2_out, not_1_out, or_1_out,
       subtractor_1_out, subtractor_2_out, xor_1_out;

  Adder adder_1 (.a(A), .b(B), .out(adder_1_out));  // open: cin, cout
  Adder adder_2 (.a(A), .b(8'h1), .out(adder_2_out));  // open: cin, cout
  Subtractor subtractor_1 (.a(A), .b(B), .out(subtractor_1_out));  // open: bin, bout
  Subtractor subtractor_2 (.a(A), .b(8'h1), .out(subtractor_2_out));  // open: bin, bout
  assign and_1_out = A & B;  // AND_Gate and_1, 8 bits wide
  assign or_1_out = A | B;  // OR_Gate or_1, 8 bits wide
  assign not_1_out = ~A;  // NOT_Gate not_1, 8 bits wide
  assign xor_1_out = A ^ B;  // XOR_Gate xor_1, 8 bits wide
  Multiplexer #(.select(2), .width(8)) multiplexer_1 (
    .in0(adder_1_out), .in1(adder_2_out), .in2(subtractor_1_out), .in3(subtractor_2_out),
    .out(multiplexer_1_out), .sel(OP[1:0]));
  Multiplexer #(.select(2), .width(8)) multiplexer_2 (
    .in0(and_1_out), .in1(or_1_out), .in2(not_1_out), .in3(xor_1_out), .out(multiplexer_2_out), .sel(OP[1:0]));
  Multiplexer #(.width(8)) multiplexer_3 (.in0(multiplexer_1_out), .in1(multiplexer_2_out), .out(R), .sel(OP[2]));
  nor nor_1 (Z, R[0], R[1], R[2], R[3], R[4], R[5], R[6], R[7]);
endmodule
